// Logisim project cpu.circ as structural Verilog: 4 circuits, main circuit CPU
module CPU (
  input  [15:0] From_Instr_Mem,
  input  clk,
  output [15:0] r0,
  output [15:0] r1,
  output [15:0] r2,
  output [15:0] r3,
  output [15:0] Display_0,
  output [15:0] Display_1,
  output [15:0] Data_Mem_Data,
  output [15:0] To_Instr_Mem,
  output [15:0] Data_Mem_Addr,
  output Data_Mem_Write
);

  wire instruction_decoder_1_out_6, instruction_decoder_1_regdest, register_file_1_p1, register_file_1_p15,
       register_file_1_p16;
  wire [1:0] instruction_decoder_1_out_3, instruction_decoder_1_out_4, instruction_decoder_1_out_5,
       multiplexer_1_out;
  wire [15:0] arithmetic_logic_unit_1_result, data_memory_1_dataout, multiplexer_2_out, register_file_1_p13,
       register_file_1_p14, undriven, WriteData;

  Instruction_Decoder instruction_decoder_1 (
    .RegDest(instruction_decoder_1_regdest), .out_3(instruction_decoder_1_out_3),
    .out_4(instruction_decoder_1_out_4), .out_5(instruction_decoder_1_out_5),
    .out_6(instruction_decoder_1_out_6));  // open: in_1
  Multiplexer #(.width(2), .enable("false")) multiplexer_1 (
    .in0(instruction_decoder_1_out_4), .in1(instruction_decoder_1_out_5), .out(multiplexer_1_out),
    .sel(instruction_decoder_1_regdest));
  // Register_File register_file_1: pin names not known; wires that end beside it: register_file_1_p1, multiplexer_1_out, instruction_decoder_1_out_5, instruction_decoder_1_out_3, WriteData, instruction_decoder_1_out_6, register_file_1_p1, r0, r1, clk, r2, r3, register_file_1_p13, register_file_1_p14, register_file_1_p15, register_file_1_p16
  Arithmetic_Logic_Unit arithmetic_logic_unit_1 (
    .X(register_file_1_p13), .RESULT(arithmetic_logic_unit_1_result), .Y(multiplexer_2_out));  // open: Switch__S, Equal, Signed_Overflow
  Multiplexer #(.width(16), .enable("false")) multiplexer_2 (
    .in0(register_file_1_p14), .out(multiplexer_2_out));  // open: in1, sel
  Multiplexer #(.width(16), .enable("false")) multiplexer_3 (
    .in0(data_memory_1_dataout), .in1(arithmetic_logic_unit_1_result), .out(WriteData),
    .sel(register_file_1_p16));
  Data_Memory data_memory_1 (
    .DataIn(arithmetic_logic_unit_1_result), .Address(undriven), .DataOut(data_memory_1_dataout),
    .MemWrite(Data_Mem_Write));  // open: Reset

  // Other names for the same wires on the sheet: d0[15:0] = Display_0; d1[15:0] = Display_1;
  //   MemWrite = Data_Mem_Write

  // Notes on the sheet:
  //   This is the current PC that you need to send as OUTPUT
  //   This is the instruction that you would receive as INPUT
  //   rt
  //   This is a CLK that is an INPUT driven from the harness.
  //   Remember, this circuit is loaded from the harness to be tested!
  //   DO NOT CHANGE THE LOCATIONS OF THE INPUTS OR OUTPUTS! IF YOU DO SO, YOU NEED TO MAKE SURE THE PINS ARE IN THE RIGHT PLACES!
  //   RegDest
  //   rd
  //   rs
  //   RegWrite
  //   These are OUTPUTS of the circuit
  //   These are OUTPUTS of the circuit
endmodule

module Data_Memory (
  input  [15:0] DataIn,
  input  [15:0] Address,
  input  Reset,
  input  MemWrite,
  output [15:0] DataOut
);

  wire clk_out, not_1_out;

  Clock clk (.out(clk_out));
  assign DataOut = MemWrite ? DataIn : 16'bz;  // Controlled_Buffer controlled_buffer_1
  RAM #(.addrWidth(16), .dataWidth(16)) ram_1 (
    .addr(Address), .data(DataOut), .sel(1'b1), .clk(clk_out), .ld(not_1_out), .clr(Reset));
  not not_1 (not_1_out, MemWrite);
endmodule

module Instruction_Decoder (
  input  [15:0] in_1,
  output RegDest,
  output [1:0] out_3,
  output [1:0] out_4,
  output [1:0] out_5,
  output out_6
);

  wire [3:0] bitselector_1_out;
  wire [15:0] demultiplexer_1_out0;

  BitSelector #(.width(16), .group(4)) bitselector_1 (.in(in_1), .out(bitselector_1_out), .sel(2'b11));
  Demultiplexer #(.select(4), .width(16), .enable("false")) demultiplexer_1 (
    .out0(demultiplexer_1_out0), .in(in_1), .sel(bitselector_1_out));  // open: out1, out2, out3, out4, out5, out6, out7, out8, out9, out10, out11, out12, out13, out14, out15
  R_type_Instruction_Decode r_type_instruction_decode_1 (
    .in_1(demultiplexer_1_out0), .rd(out_4), .rt(out_5), .rs(out_3), .RegWrite(out_6), .RegDest(RegDest));

  // Other names for the same wires on the sheet: rd[1:0] = out_4; RegWrite = out_6; rs[1:0] = out_3; rt[1:0] = out_5

  // Notes on the sheet:
  //   0: write to rd
  //   1: write to rt
endmodule

module R_type_Instruction_Decode (
  input  [15:0] in_1,
  output [1:0] rd,
  output [1:0] rt,
  output [1:0] rs,
  output RegWrite,
  output RegDest
);

  BitSelector #(.width(16), .group(2)) bitselector_1 (.in(in_1), .out(rd), .sel(3'b011));
  BitSelector #(.width(16), .group(2)) bitselector_2 (.in(in_1), .out(rt), .sel(3'b100));
  BitSelector #(.width(16), .group(2)) bitselector_3 (.in(in_1), .out(rs), .sel(3'b101));

  assign RegDest = 1'b0;
  assign RegWrite = 1'b1;

  // Notes on the sheet:
  //   (enable write to register)
  //   (select rd as destination register)
endmodule
